// Logisim project CIRCUITO_01.circ as structural Verilog: 1 circuit, main circuit main
module main (
  input  [3:0] in_1,
  input  \HABILITA_GRAVAÇÃO 
);

  wire clock_1_out, CLOCK_2_out, registerfile_1_p1, registerfile_1_p7, registerfile_1_p8;
  wire [31:0] adder_1_out, mipsprogramrom_1_p2, register_1_q;

  Adder #(.width(32)) adder_1 (.a(register_1_q), .b(32'h4), .out(adder_1_out));  // open: cin, cout
  Register #(.width(32)) register_1 (.D(adder_1_out), .Q(register_1_q), .clk(clock_1_out));  // open: en, clr
  Clock clock_1 (.out(clock_1_out));
  // MIPSProgramROM mipsprogramrom_1: pin names not known; wires that end beside it: register_1_q, mipsprogramrom_1_p2
  Clock CLOCK_2 (.out(CLOCK_2_out));
  // RegisterFile registerfile_1: pin names not known; wires that end beside it: registerfile_1_p1, CLOCK_2_out, \HABILITA_GRAVAÇÃO , mipsprogramrom_1_p2[15:11], mipsprogramrom_1_p2[25:21], mipsprogramrom_1_p2[20:16], registerfile_1_p7, registerfile_1_p8
  // Mips_ALU mips_alu_1: pin names not known; wires that end beside it: registerfile_1_p7, registerfile_1_p8, in_1, registerfile_1_p1
endmodule
