// Logisim project CIRCUITO_01.circ as structural Verilog: 1 circuit, main circuit main
module main (
  input  MEM_TO_REG,
  input  LOAD,
  input  [3:0] ALU_OP
);

  wire ALU_SRC, and_1_out, CLK, REG_DEST, REG_W, registerfile_1_p7, STORE;
  wire [4:0] multiplexer_1_out;
  wire [31:0] adder_1_out, bit_extender_1_out, mips_alu_1_p4, mips_ram_1_p5, mipsprogramrom_1_p2,
       multiplexer_2_out, register_1_q, registerfile_1_p1, registerfile_1_p8;

  Clock clock_1 (.out(CLK));
  Adder #(.width(32)) adder_1 (.a(register_1_q), .b(32'h4), .out(adder_1_out));  // open: cin, cout
  Register #(.width(32)) register_1 (.D(adder_1_out), .clk(CLK), .Q(register_1_q));  // open: en, clr
  // MIPSProgramROM mipsprogramrom_1: pin names not known; wires that end beside it: register_1_q, mipsprogramrom_1_p2, mipsprogramrom_1_p2[27], mipsprogramrom_1_p2[28]
  Multiplexer #(.width(5), .enable("false")) multiplexer_1 (
    .in0(mipsprogramrom_1_p2[15:11]), .in1(mipsprogramrom_1_p2[20:16]), .out(multiplexer_1_out),
    .sel(REG_DEST));
  and and_1 (and_1_out, mipsprogramrom_1_p2[26], ~mipsprogramrom_1_p2[27], ~mipsprogramrom_1_p2[28], mipsprogramrom_1_p2[29], ~mipsprogramrom_1_p2[30], ~mipsprogramrom_1_p2[31]);  // AND_Gate
  and and_2 (STORE, mipsprogramrom_1_p2[26], mipsprogramrom_1_p2[27], ~mipsprogramrom_1_p2[28], mipsprogramrom_1_p2[29], ~mipsprogramrom_1_p2[30], mipsprogramrom_1_p2[31]);  // AND_Gate
  or or_1 (ALU_SRC, and_1_out, STORE);
  or or_2 (REG_DEST, and_1_out, STORE);
  or or_3 (REG_W, and_1_out, STORE);
  // RegisterFile registerfile_1: pin names not known; wires that end beside it: registerfile_1_p1, CLK, REG_W, multiplexer_1_out, mipsprogramrom_1_p2[25:21], mipsprogramrom_1_p2[20:16], registerfile_1_p7, registerfile_1_p8
  assign bit_extender_1_out = {{16{1'b0}}, mipsprogramrom_1_p2[15:0]};  // Bit_Extender bit_extender_1
  Multiplexer #(.width(32), .enable("false")) multiplexer_2 (
    .in0(registerfile_1_p8), .in1(bit_extender_1_out), .out(multiplexer_2_out), .sel(ALU_SRC));
  // Mips_ALU mips_alu_1: pin names not known; wires that end beside it: registerfile_1_p7, multiplexer_2_out, ALU_OP, mips_alu_1_p4, registerfile_1_p8
  Multiplexer #(.width(32), .enable("false")) multiplexer_3 (
    .in0(mips_alu_1_p4), .in1(mips_ram_1_p5), .out(registerfile_1_p1), .sel(MEM_TO_REG));
  // MIPS_RAM mips_ram_1: pin names not known; wires that end beside it: mips_alu_1_p4[19:0], STORE, CLK, LOAD, mips_ram_1_p5

  // Notes on the sheet:
  //   contents of mipsprogramrom_1 (hex, n*v repeats v):
  //   addiu $2, $0, 0xCAFE sw $2, 0($1)
  //   R
  //   I
  //   ADDIU
  //   STORE
  //   R
  //   I
endmodule
