// Logisim project CIRCUITO_02.circ as structural Verilog: 1 circuit, main circuit main
module main (
  input  MEM_TO_REG,
  input  STORE,
  input  REG_DEST,
  input  [3:0] ALU_OP,
  input  ALU_SRC,
  input  \HABILITA_GRAVAÇÃO 
);

  wire clock_1_out, CLOCK_2_out, registerfile_1_p7;
  wire [4:0] multiplexer_1_out;
  wire [31:0] adder_1_out, bit_extender_1_out, mips_alu_1_p4, mips_ram_1_p3, mipsprogramrom_1_p2,
       multiplexer_2_out, register_1_q, registerfile_1_p1, registerfile_1_p8;

  Adder #(.width(32)) adder_1 (.a(register_1_q), .b(32'h4), .out(adder_1_out));  // open: cin, cout
  Register #(.width(32)) register_1 (.D(adder_1_out), .Q(register_1_q), .clk(clock_1_out));  // open: en, clr
  Clock clock_1 (.out(clock_1_out));
  // MIPSProgramROM mipsprogramrom_1: pin names not known; wires that end beside it: register_1_q, mipsprogramrom_1_p2
  Multiplexer #(.width(5)) multiplexer_1 (
    .in0(mipsprogramrom_1_p2[15:11]), .in1(mipsprogramrom_1_p2[20:16]), .out(multiplexer_1_out),
    .sel(REG_DEST));  // open: en
  Clock CLOCK_2 (.out(CLOCK_2_out));
  // RegisterFile registerfile_1: pin names not known; wires that end beside it: registerfile_1_p1, CLOCK_2_out, \HABILITA_GRAVAÇÃO , multiplexer_1_out, mipsprogramrom_1_p2[25:21], mipsprogramrom_1_p2[20:16], registerfile_1_p7, registerfile_1_p8
  assign bit_extender_1_out = {{16{1'b0}}, mipsprogramrom_1_p2[15:0]};  // Bit_Extender bit_extender_1
  Multiplexer #(.width(32)) multiplexer_2 (
    .in0(registerfile_1_p8), .in1(bit_extender_1_out), .out(multiplexer_2_out), .sel(ALU_SRC));  // open: en
  // Mips_ALU mips_alu_1: pin names not known; wires that end beside it: registerfile_1_p7, multiplexer_2_out, ALU_OP, mips_alu_1_p4, registerfile_1_p8
  Multiplexer #(.width(32)) multiplexer_3 (
    .in0(mips_alu_1_p4), .in1(mips_ram_1_p3), .out(registerfile_1_p1), .sel(MEM_TO_REG));  // open: en
  // MIPS_RAM mips_ram_1: pin names not known; wires that end beside it: mips_alu_1_p4[19:0], STORE, mips_ram_1_p3

  // Notes on the sheet:
  //   R
  //   I
  //   R
  //   I
endmodule
